# Fritzing sketch DoggyDoorCircuit (saved by Fritzing 0.9.3b)
breadboards: 1

parts:
  Part1 = Arduino Nano (Rev3.0)
  M1 = DC Motor
  Sensor_Closed = Reed switch [package=THT]
  Sensor_Open = Reed switch [package=THT]
  V2 = DC Power [voltage=5]
  V4 = DC Power [voltage=12V]
  IC1 = H-Bridge [package=THT]
  U1 = RELAY [package=relay-t9a-2]
  R1 = Resistor [tolerance=±5% resistance=5k package="0402 [SMD]"]
  R2 = Resistor [tolerance=±5% resistance=5k package="0603 [SMD]"]
  Input_Signal = SPST Switch [package=switch-spdt_lock.007s]
  U2 = 74HC04_HEX_INVERTER [package=dil14]

nets:
  N1: Part1.GND, V2.V-
  N2: Part1.D3, Sensor_Closed.pin_1, R2.Pin_0
  N3: Part1.D4, Sensor_Open.pin_1, R1.Pin_0
  N4: Part1.D5, Input_Signal.P
  N5: Part1.D10, IC1.2A, U2.1A
  N6: Part1.D11/MOSI, U1.COIL1
  VIN: Part1.VIN, Sensor_Closed.pin_2, Sensor_Open.pin_2, V2.V+, IC1.1_2EN, Input_Signal.O, U2.VCC
  N7: Part1.5V, U1.COIL2
  N8: M1.pin_1, IC1.1Y
  N9: M1.pin_2, IC1.2Y
  N10: V4.V+, U1.NO
  GND1: V4.V-, IC1.GND1, IC1.GND2, Input_Signal.S, U2.GND
  N11: IC1.1A, U2.1Y
  N12: IC1.VCC2, U1.MAIN
  GND: R1.Pin_1, R2.Pin_1

notes:
  Red = 5v
  Yellow = 12v
  Green = Output
  Purple = Input
  Black = Ground
